# Fritzing sketch arpy_lcd_res (saved by Fritzing 0.7.11b)
breadboards: 1

parts:
  Arduino1 = Arduino
  R1 = 10k Ω Resistor [package=THT]
  LCD1 = LCD screen

nets:
  N1: Arduino1.D12, LCD1.RS
  N2: Arduino1.D11, LCD1.E
  N3: Arduino1.D5, LCD1.DB4
  N4: Arduino1.D4, LCD1.DB5
  N5: Arduino1.D3, LCD1.DB6
  N6: Arduino1.D2, LCD1.DB7
  +5V: Arduino1.+5V, R1.Pin_0, LCD1.VDD
  GND: Arduino1.GND, R1.Pin_1, LCD1.VSS, LCD1.V0, LCD1.R/W
