# Fritzing sketch arpy_led (saved by Fritzing 0.7.11b)
breadboards: 1

parts:
  Arduino1 = Arduino
  LED1 = LED - 3mm [color="Red (633nm)" package="3 mm [THT]"]
  R1 = Resistor [tolerance=±5% resistance=220 package="0805 [SMD]"]

nets:
  N1: Arduino1.D9, R1.Pin_0
  N2: Arduino1.GND, LED1.cathode
  N3: LED1.anode, R1.Pin_1
